# Fritzing sketch adsr85_control (saved by Fritzing 0.9.3b)
circuit board: 9.2cm x 9.2cm
breadboards: 1

parts:
  J1 = 3.5mm Switch Jack [part_number=PJ301M-12]
  R1 = Rotary Potentiometer (Large) [maximum_resistance=10kΩ package=THT]
  J2 = 3.5mm Switch Jack [part_number=PJ301M-12]
  R2 = Rotary Potentiometer (Large) [maximum_resistance=10kΩ package=THT]
  J3 = 3.5mm Switch Jack [part_number=PJ301M-12]
  R3 = Rotary Potentiometer (Large) [maximum_resistance=10kΩ package=THT]
  J4 = 3.5mm Switch Jack [part_number=PJ301M-12]
  R4 = Rotary Potentiometer (Large) [maximum_resistance=10kΩ package=THT]
  R5 = Rotary Potentiometer (Large) [maximum_resistance=10kΩ package=THT]
  J5 = 3.5mm Switch Jack [part_number=PJ301M-12]
  J6 = 3.5mm Switch Jack [part_number=PJ301M-12]
  J8 = female pin header, 4 pins [form="♀ (female)"]
  J3_2 = female pin header, 1 pin [form="♀ (female)"]
  J2_2 = female pin header, 1 pin [form="♀ (female)"]
  J1_2 = female pin header, 1 pin [form="♀ (female)"]
  J4_2 = female pin header, 1 pin [form="♀ (female)"]

nets:
  GND: J1.Pin_1
  N1: J1.Pin_2, R1.wiper
  N2: J1.Pin_3, J8.pin3
  N3: R1.leg2, R2.leg2, R3.leg2, R4.leg2, J4_2.pin1
  N4: J2.Pin_2, R2.wiper
  N5: J2.Pin_3, J8.pin2
  N6: J3.Pin_2, R3.wiper
  N7: J3.Pin_3, J8.pin1
  N8: J4.Pin_2, R4.wiper
  N9: J4.Pin_3, J1_2.pin1
  N10: R5.wiper, J5.Pin_3
  N11: R5.leg2, J3_2.pin1
  N12: J6.Pin_3, J2_2.pin1

notes:
  A
  D
  S
  R
  OUT
  GATE
  Depth

custom parts:
  3.5mm Switch Jack: Thonkiconn 3.5mm switching Jack
